# Fritzing sketch Circuit_Schematic (saved by Fritzing 0.9.3b)
breadboards: 1

parts:
  IC1 = ULN2003A [package="DIP16 [THT]"]
  M1 = Stepper Motor - Unipolar
  Switch_1 = Pushbutton [package=THT]
  Switch_2 = Pushbutton [package=THT]
  Part1 = Arduino Uno (Rev3)
  Power_Supply = DC Power [voltage=5]

nets:
  N1: IC1.In_1, Part1.D2
  N2: IC1.In_2, Part1.D3_PWM
  N3: IC1.In_3, Part1.D4
  N4: IC1.In_4, Part1.D5_PWM
  N5: IC1.COM_-_Common, M1.COMMON_1, M1.COMMON_2, Part1.VIN, Power_Supply.V+
  N6: IC1.Out_4, M1.D
  N7: IC1.Out_3, M1.C
  N8: IC1.Out_2, M1.B
  N9: IC1.Out_1, M1.A
  N10: Switch_1.leg0, Switch_2.leg0, Part1.GND, Power_Supply.V-
  N11: Switch_1.leg1, Part1.D7
  N12: Switch_2.leg1, Part1.D6_PWM
